// Logisim project Cache.circ as structural Verilog: 9 circuits, main circuit implementation
module implementation (
  input  [9:0] CpuAddressIn,
  input  CpuReadIn,
  input  CpuWriteIn,
  input  [7:0] CpuWriteValueIn,
  input  [31:0] LineFromMemIn,
  input  ClkIn,
  output ReadyOut,
  output DidContainOut,
  output [7:0] ByteReadOut,
  output [7:0] MemAddressOut,
  output MemReadOut,
  output MemWriteOut,
  output [31:0] Line2MemOut,
  output [5:0] state
);

  wire age_initial, age_update, cmd_store, dirty, dirty_0, dirty_1, dirty_2, line_update_en, mem_data_store,
       r_reg, valid_0, valid_1, valid_2, w_reg;
  wire [1:0] age_0, age_1, age_2, bitfinder_1_index, bitfinder_2_index;
  wire [2:0] hit_way, old_vec;
  wire [6:0] tag_0, tag_1, tag_2;
  wire [7:0] byte_hit, byte_mem, CpuWriteValue_reg;
  wire [7:1] MemAddress_w;
  wire [9:0] CpuAddress_reg;
  wire [31:0] line_hit, line_old, LineFromMem_reg;

  Register #(.width(32)) register_1 (
    .D(LineFromMemIn), .en(mem_data_store), .clk(ClkIn), .Q(LineFromMem_reg), .clr(1'b0));
  Multiplexer #(.enable("false"), .select(2), .width(8)) multiplexer_1 (
    .in0(LineFromMemIn[7:0]), .in1(LineFromMemIn[15:8]), .in2(LineFromMemIn[23:16]),
    .in3(LineFromMemIn[31:24]), .out(byte_mem), .sel(CpuAddress_reg[1:0]));
  Multiplexer #(.enable("false"), .select(2), .width(7)) multiplexer_2 (
    .in0(tag_0), .in1(tag_1), .in2(tag_2), .out(MemAddress_w), .sel(bitfinder_1_index));  // open: in3
  BitFinder #(.width(3)) bitfinder_1 (.in(old_vec), .index(bitfinder_1_index));  // open: found
  set_top set (
    .line_from_mem(LineFromMemIn), .cpu_byte(CpuWriteValue_reg), .old_vec(old_vec),
    .update_en(line_update_en), .hit_way(hit_way), .clk(ClkIn), .w_reg(w_reg), .cpu_address(CpuAddress_reg),
    .index(CpuAddress_reg[2]), .valid_0(valid_0), .valid_1(valid_1), .valid_2(valid_2), .dirty_0(dirty_0),
    .dirty_1(dirty_1), .dirty_2(dirty_2), .tag_0(tag_0), .tag_1(tag_1), .tag_2(tag_2), .byte_hit(byte_hit),
    .line_old(line_old), .line_hit(line_hit));
  hit_cmp hit_judge (
    .hit_way(hit_way), .hit(DidContainOut), .valid_0(valid_0), .valid_1(valid_1), .valid_2(valid_2),
    .index(CpuAddress_reg[2]), .tag(CpuAddress_reg[9:3]), .tag_1(tag_1), .tag_2(tag_2), .tag_0(tag_0));
  LRU Age_reg (
    .index(CpuAddress_reg[2]), .hit_way(hit_way), .hit(DidContainOut), .update_en(age_update), .clk(ClkIn),
    .age_initial(age_initial), .age_0(age_0), .age_1(age_1), .age_2(age_2), .old_vec(old_vec));
  // Probe on ByteReadOut
  // Probe on Line2MemOut
  Multiplexer #(.enable("false"), .width(8)) multiplexer_3 (
    .in0({MemAddress_w, CpuAddress_reg[2]}), .in1(CpuAddress_reg[9:2]), .out(MemAddressOut), .sel(MemReadOut));
  Register #(.width(10)) cmd_reg (.D(CpuAddressIn), .en(cmd_store), .clk(ClkIn), .Q(CpuAddress_reg), .clr(1'b0));
  Register #(.width(1)) register_2 (.D(CpuWriteIn), .en(cmd_store), .clk(ClkIn), .Q(w_reg), .clr(1'b0));
  Multiplexer #(.enable("false"), .width(8)) multiplexer_4 (
    .in0(byte_mem), .in1(byte_hit), .out(ByteReadOut), .sel(DidContainOut));
  Multiplexer #(.enable("false"), .width(32)) multiplexer_5 (
    .in0(line_old), .in1(line_hit), .out(Line2MemOut), .sel(DidContainOut));
  FSM Control (
    .wr(w_reg), .dirty(dirty), .rd(r_reg), .w_en(w_reg), .hit(DidContainOut), .clk(ClkIn),
    .rd_mem(MemReadOut), .age_initial(age_initial), .wr_mem(MemWriteOut), .cur_state(state),
    .ready(ReadyOut), .cmd_store(cmd_store), .mem_data_store(mem_data_store), .age_update(age_update),
    .line_update_en(line_update_en));
  // Probe on w_reg
  // Probe on CpuWriteValue_reg
  // Probe on r_reg
  // Probe on CpuAddress_reg
  Register #(.width(1)) register_3 (.D(CpuReadIn), .en(cmd_store), .clk(ClkIn), .Q(r_reg), .clr(1'b0));
  Register register_4 (.D(CpuWriteValueIn), .en(cmd_store), .clk(ClkIn), .Q(CpuWriteValue_reg));  // open: clr
  BitFinder #(.width(3)) bitfinder_2 (.in(old_vec), .index(bitfinder_2_index));  // open: found
  // Probe on CpuAddress_reg[1:0]
  // Probe on CpuAddress_reg[2]
  // Probe on CpuAddress_reg[9:3]
  Multiplexer #(.enable("false"), .select(2)) multiplexer_6 (
    .in0(dirty_0), .in1(dirty_1), .in2(dirty_2), .out(dirty), .sel(bitfinder_2_index));  // open: in3

  // Other names for the same wires on the sheet: clk = ClkIn; CpuAddress[9:0] = CpuAddressIn;
  //   offset[1:0] = CpuAddress_reg[1:0]; index = CpuAddress_reg[2]; MemAddress_r[7:0] = CpuAddress_reg[9:2];
  //   MemAddress_w[0] = CpuAddress_reg[2]; tag[6:0] = CpuAddress_reg[9:3]; CpuRead = CpuReadIn; CpuWrite = CpuWriteIn;
  //   CpuWriteValue[7:0] = CpuWriteValueIn; DidContain = DidContainOut; hit = DidContainOut;
  //   LineFromMem[31:0] = LineFromMemIn; MemAddress[7:0] = MemAddressOut; MemRead = MemReadOut;
  //   MemWrite = MemWriteOut; Ready = ReadyOut; ByteRead[7:0] = ByteReadOut; SelectedSetByteRead[7:0] = ByteReadOut;
  //   Line2Mem[31:0] = Line2MemOut; SelectedSetLine2Mem[31:0] = Line2MemOut

  // Notes on the sheet:
  //   Shuhao Gao: 919412501
  //   Miou Lu: 918657325
endmodule

module set_top (
  input  [31:0] line_from_mem,
  input  [7:0] cpu_byte,
  input  [2:0] old_vec,
  input  update_en,
  input  [2:0] hit_way,
  input  clk,
  input  w_reg,
  input  [9:0] cpu_address,
  input  index,
  output valid_0,
  output valid_1,
  output valid_2,
  output dirty_0,
  output dirty_1,
  output dirty_2,
  output [6:0] tag_0,
  output [6:0] tag_1,
  output [6:0] tag_2,
  output [7:0] byte_hit,
  output [31:0] line_old,
  output [31:0] line_hit
);

  wire dirty_set0_0, dirty_set0_1, dirty_set0_2, dirty_set1_0, dirty_set1_1, dirty_set1_2, not_1_out,
       valid_set0_0, valid_set0_1, valid_set0_2, valid_set1_0, valid_set1_1, valid_set1_2;
  wire [6:0] tag_set0_0, tag_set0_1, tag_set0_2, tag_set1_0, tag_set1_1, tag_set1_2;
  wire [7:0] byte_set0, byte_set1;
  wire [31:0] line_hit_0, line_hit_1, line_old_0, line_old_1;

  not not_1 (not_1_out, index);
  sub_set set0 (
    .tag_0(tag_set0_0), .tag_1(tag_set0_1), .tag_2(tag_set0_2), .line_old(line_old_0), .line_hit(line_hit_0),
    .byte_hit(byte_set0), .valid_0(valid_set0_0), .valid_1(valid_set0_1), .valid_2(valid_set0_2),
    .dirty_0(dirty_set0_0), .dirty_1(dirty_set0_1), .dirty_2(dirty_set0_2), .index(not_1_out),
    .hit_way(hit_way), .clk(clk), .line_from_mem(line_from_mem), .w_en(w_reg), .cpu_addr(cpu_address),
    .old_vec(old_vec), .update_en(update_en), .cpu_byte(cpu_byte));
  sub_set set1 (
    .tag_0(tag_set1_0), .tag_1(tag_set1_1), .tag_2(tag_set1_2), .line_old(line_old_1), .line_hit(line_hit_1),
    .byte_hit(byte_set1), .valid_0(valid_set1_0), .valid_1(valid_set1_1), .valid_2(valid_set1_2),
    .dirty_0(dirty_set1_0), .dirty_1(dirty_set1_1), .dirty_2(dirty_set1_2), .index(index), .hit_way(hit_way),
    .clk(clk), .line_from_mem(line_from_mem), .w_en(w_reg), .cpu_addr(cpu_address), .old_vec(old_vec),
    .update_en(update_en), .cpu_byte(cpu_byte));
  Multiplexer #(.enable("false"), .width(32)) multiplexer_1 (
    .in0(line_old_0), .in1(line_old_1), .out(line_old), .sel(index));
  Multiplexer #(.enable("false"), .width(32)) multiplexer_2 (
    .in0(line_hit_0), .in1(line_hit_1), .out(line_hit), .sel(index));
  Multiplexer #(.enable("false"), .width(8)) multiplexer_3 (
    .in0(byte_set0), .in1(byte_set1), .out(byte_hit), .sel(index));
  Multiplexer #(.enable("false")) multiplexer_4 (.in0(valid_set0_0), .in1(valid_set1_0), .out(valid_0), .sel(index));
  Multiplexer #(.enable("false")) multiplexer_5 (.in0(valid_set0_1), .in1(valid_set1_1), .out(valid_1), .sel(index));
  Multiplexer #(.enable("false")) multiplexer_6 (.in0(valid_set0_2), .in1(valid_set1_2), .out(valid_2), .sel(index));
  Multiplexer #(.enable("false")) multiplexer_7 (.in0(dirty_set0_0), .in1(dirty_set1_0), .out(dirty_0), .sel(index));
  Multiplexer #(.enable("false")) multiplexer_8 (.in0(dirty_set0_1), .in1(dirty_set1_1), .out(dirty_1), .sel(index));
  Multiplexer #(.enable("false")) multiplexer_9 (.in0(dirty_set0_2), .in1(dirty_set1_2), .out(dirty_2), .sel(index));
  Multiplexer #(.enable("false"), .width(7)) multiplexer_10 (
    .in0(tag_set0_0), .in1(tag_set1_0), .out(tag_0), .sel(index));
  Multiplexer #(.enable("false"), .width(7)) multiplexer_11 (
    .in0(tag_set0_1), .in1(tag_set1_1), .out(tag_1), .sel(index));
  Multiplexer #(.enable("false"), .width(7)) multiplexer_12 (
    .in0(tag_set0_2), .in1(tag_set1_2), .out(tag_2), .sel(index));

  // Other names for the same wires on the sheet: CpuAddress_reg[9:0] = cpu_address
endmodule

module sub_set (
  input  [2:0] hit_way,
  input  [2:0] old_vec,
  input  update_en,
  input  clk,
  input  w_en,
  input  [7:0] cpu_byte,
  input  [31:0] line_from_mem,
  input  [9:0] cpu_addr,
  input  index,
  output [7:0] byte_hit,
  output valid_0,
  output valid_1,
  output valid_2,
  output dirty_0,
  output dirty_1,
  output dirty_2,
  output [6:0] tag_0,
  output [6:0] tag_1,
  output [6:0] tag_2,
  output [31:0] line_old,
  output [31:0] line_hit
);

  wire and_1_out, and_2_out, and_3_out, and_4_out, and_5_out, and_6_out, and_7_out, and_8_out, and_9_out,
       and_10_out, and_11_out, and_12_out, and_13_out, and_14_out, and_15_out, and_19_out, and_20_out,
       and_21_out, dirty_0_en, dirty_0_next, dirty_1_en, dirty_1_next, dirty_2_en, dirty_2_next, hit,
       multiplexer_1_out, multiplexer_2_out, multiplexer_3_out, multiplexer_4_out, multiplexer_5_out,
       multiplexer_6_out, not_1_out, not_2_out, not_3_out, or_2_out, or_3_out, or_4_out, or_5_out, or_6_out,
       or_7_out, or_9_out, or_10_out, or_11_out, or_12_out, or_13_out, or_14_out, valid_0_en, valid_1_en,
       valid_2_en;
  wire [1:0] bitfinder_2_index, way_sel;
  wire [7:0] block_0_byte_0, block_0_byte_1, block_0_byte_2, block_0_byte_3, block_1_byte_0, block_1_byte_1,
       block_1_byte_2, block_1_byte_3, block_2_byte_0, block_2_byte_1, block_2_byte_2, block_2_byte_3,
       multiplexer_10_out, multiplexer_11_out, multiplexer_12_out;

  or or_1 (hit, hit_way[0], hit_way[1], hit_way[2]);
  Register #(.width(1)) register_1 (.D(1'b1), .en(valid_0_en), .clk(clk), .Q(valid_0), .clr(1'b0));
  Register #(.width(1)) register_2 (.D(1'b1), .en(valid_1_en), .clk(clk), .Q(valid_1), .clr(1'b0));
  Register #(.width(1)) register_3 (.D(1'b1), .en(valid_2_en), .clk(clk), .Q(valid_2), .clr(1'b0));
  Register #(.width(7)) register_4 (.D(cpu_addr[9:3]), .en(and_19_out), .clk(clk), .Q(tag_0));  // open: clr
  Register #(.width(7)) register_5 (.D(cpu_addr[9:3]), .en(and_20_out), .clk(clk), .Q(tag_1));  // open: clr
  Register #(.width(7)) register_6 (.D(cpu_addr[9:3]), .en(and_21_out), .clk(clk), .Q(tag_2));  // open: clr
  // Probe on tag_0
  // Probe on tag_1
  // Probe on tag_2
  // Probe on dirty_0
  Register #(.width(1)) register_7 (.D(dirty_0_next), .en(dirty_0_en), .clk(clk), .Q(dirty_0), .clr(1'b0));
  Register #(.width(1)) register_8 (.D(dirty_1_next), .en(dirty_1_en), .clk(clk), .Q(dirty_1), .clr(1'b0));
  // Probe on dirty_2
  Register #(.width(1)) register_9 (.D(dirty_2_next), .en(dirty_2_en), .clk(clk), .Q(dirty_2), .clr(1'b0));
  and and_1 (and_1_out, ~hit, old_vec[0]);  // AND_Gate
  and and_2 (and_2_out, ~hit, old_vec[1]);  // AND_Gate
  and and_3 (and_3_out, ~hit, old_vec[2]);  // AND_Gate
  // Probe on dirty_1
  and and_4 (and_4_out, ~hit, ~old_vec[2]);  // AND_Gate
  and and_5 (and_5_out, old_vec[0], ~hit);  // AND_Gate
  or or_2 (or_2_out, hit_way[0], and_1_out);
  and and_6 (and_6_out, ~hit, ~old_vec[0]);  // AND_Gate
  or or_3 (or_3_out, hit_way[1], and_2_out);
  and and_7 (and_7_out, ~hit, ~old_vec[1]);  // AND_Gate
  or or_4 (or_4_out, hit_way[2], and_3_out);
  or or_5 (or_5_out, and_4_out, and_11_out);
  and and_8 (and_8_out, old_vec[1], ~hit);  // AND_Gate
  and and_9 (and_9_out, old_vec[2], ~hit);  // AND_Gate
  Multiplexer #(.enable("false")) multiplexer_1 (
    .in0(or_2_out), .in1(dirty_0), .out(multiplexer_1_out), .sel(or_6_out));
  or or_6 (or_6_out, and_6_out, and_15_out);
  Multiplexer #(.enable("false")) multiplexer_2 (
    .in0(or_3_out), .in1(dirty_1), .out(multiplexer_2_out), .sel(or_7_out));
  or or_7 (or_7_out, and_7_out, and_10_out);
  and and_10 (and_10_out, hit, ~hit_way[1]);  // AND_Gate
  Multiplexer #(.enable("false")) multiplexer_3 (
    .in0(or_4_out), .in1(dirty_2), .out(multiplexer_3_out), .sel(or_5_out));
  and and_11 (and_11_out, hit, ~hit_way[2]);  // AND_Gate
  sub_block block_0 (
    .clk(clk), .block_from_mem(line_from_mem), .hit_block(hit), .index(index), .old(old_vec[0]),
    .line_update_en(update_en), .byte_in(cpu_byte), .offset(cpu_addr[1:0]), .hit(hit_way[0]), .wr(w_en),
    .byte_out_0(block_0_byte_0), .byte_out_1(block_0_byte_1), .byte_out_2(block_0_byte_2),
    .byte_out_3(block_0_byte_3));
  sub_block block_1 (
    .clk(clk), .block_from_mem(line_from_mem), .hit_block(hit), .index(index), .old(old_vec[1]),
    .line_update_en(update_en), .byte_in(cpu_byte), .offset(cpu_addr[1:0]), .hit(hit_way[1]), .wr(w_en),
    .byte_out_0(block_1_byte_0), .byte_out_1(block_1_byte_1), .byte_out_2(block_1_byte_2),
    .byte_out_3(block_1_byte_3));
  sub_block block_2 (
    .clk(clk), .block_from_mem(line_from_mem), .hit_block(hit), .index(index), .old(old_vec[2]),
    .line_update_en(update_en), .byte_in(cpu_byte), .offset(cpu_addr[1:0]), .hit(hit_way[2]), .wr(w_en),
    .byte_out_0(block_2_byte_0), .byte_out_1(block_2_byte_1), .byte_out_2(block_2_byte_2),
    .byte_out_3(block_2_byte_3));
  or or_8 (hit, hit_way[0], hit_way[1], hit_way[2]);
  or or_9 (or_9_out, hit_way[0], and_5_out);
  or or_10 (or_10_out, hit_way[1], and_8_out);
  or or_11 (or_11_out, hit_way[2], and_9_out);
  and and_12 (and_12_out, index, old_vec[0], update_en);
  and and_13 (and_13_out, index, old_vec[1], update_en);
  and and_14 (and_14_out, index, old_vec[2], update_en);
  or or_12 (or_12_out, hit_way[0], old_vec[0]);
  or or_13 (or_13_out, hit_way[1], old_vec[1]);
  or or_14 (or_14_out, hit_way[2], old_vec[2]);
  and and_15 (and_15_out, hit, ~hit_way[0]);  // AND_Gate
  Multiplexer #(.enable("false")) multiplexer_4 (.in0(1'b0), .in1(dirty_2), .out(multiplexer_4_out), .sel(hit));
  // Probe on valid_0_en
  and and_16 (valid_0_en, or_9_out, update_en, index);
  // Probe on valid_1_en
  and and_17 (valid_1_en, or_10_out, update_en, index);
  // Probe on valid_2_en
  and and_18 (valid_2_en, or_11_out, update_en, index);
  and and_19 (and_19_out, and_12_out, ~hit);  // AND_Gate
  Multiplexer #(.enable("false")) multiplexer_5 (.in0(1'b0), .in1(dirty_0), .out(multiplexer_5_out), .sel(hit));
  Multiplexer #(.enable("false")) multiplexer_6 (.in0(1'b0), .in1(dirty_1), .out(multiplexer_6_out), .sel(hit));
  not not_1 (not_1_out, w_en);
  Multiplexer #(.enable("false")) multiplexer_7 (
    .in0(multiplexer_3_out), .in1(multiplexer_4_out), .out(dirty_2_next), .sel(not_2_out));
  not not_2 (not_2_out, w_en);
  and and_20 (and_20_out, and_13_out, ~hit);  // AND_Gate
  and and_21 (and_21_out, and_14_out, ~hit);  // AND_Gate
  // Probe on dirty_0_en
  and and_22 (dirty_0_en, or_12_out, update_en, index);
  // Probe on dirty_1_en
  and and_23 (dirty_1_en, or_13_out, update_en, index);
  // Probe on dirty_2_en
  and and_24 (dirty_2_en, or_14_out, update_en, index);
  // Probe on dirty_0_next
  Multiplexer #(.enable("false")) multiplexer_8 (
    .in0(multiplexer_1_out), .in1(multiplexer_5_out), .out(dirty_0_next), .sel(not_3_out));
  not not_3 (not_3_out, w_en);
  // Probe on dirty_1_next
  Multiplexer #(.enable("false")) multiplexer_9 (
    .in0(multiplexer_2_out), .in1(multiplexer_6_out), .out(dirty_1_next), .sel(not_1_out));
  // Probe on dirty_2_next
  BitFinder #(.width(3)) bitfinder_1 (.in(hit_way), .index(way_sel));  // open: found
  Multiplexer #(.enable("false"), .select(2), .width(8)) multiplexer_10 (
    .in0(block_0_byte_0), .in1(block_0_byte_1), .in2(block_0_byte_2), .in3(block_0_byte_3),
    .out(multiplexer_10_out), .sel(cpu_addr[1:0]));
  Multiplexer #(.enable("false"), .select(2), .width(8)) multiplexer_11 (
    .in0(block_1_byte_0), .in1(block_1_byte_1), .in2(block_1_byte_2), .in3(block_1_byte_3),
    .out(multiplexer_11_out), .sel(cpu_addr[1:0]));
  Multiplexer #(.enable("false"), .select(2), .width(8)) multiplexer_12 (
    .in0(block_2_byte_0), .in1(block_2_byte_1), .in2(block_2_byte_2), .in3(block_2_byte_3),
    .out(multiplexer_12_out), .sel(cpu_addr[1:0]));
  Multiplexer #(.enable("false"), .select(2), .width(8)) multiplexer_13 (
    .in0(multiplexer_10_out), .in1(multiplexer_11_out), .in2(multiplexer_12_out), .out(byte_hit),
    .sel(way_sel));  // open: in3
  Multiplexer #(.enable("false"), .select(2), .width(32)) multiplexer_14 (
    .in0({block_0_byte_3, block_0_byte_2, block_0_byte_1, block_0_byte_0}),
    .in1({block_1_byte_3, block_1_byte_2, block_1_byte_1, block_1_byte_0}),
    .in2({block_2_byte_3, block_2_byte_2, block_2_byte_1, block_2_byte_0}), .out(line_old),
    .sel(bitfinder_2_index));  // open: in3
  BitFinder #(.width(3)) bitfinder_2 (.in(old_vec), .index(bitfinder_2_index));  // open: found
  Multiplexer #(.enable("false"), .select(2), .width(32)) multiplexer_15 (
    .in0({block_0_byte_3, block_0_byte_2, block_0_byte_1, block_0_byte_0}),
    .in1({block_1_byte_3, block_1_byte_2, block_1_byte_1, block_1_byte_0}),
    .in2({block_2_byte_3, block_2_byte_2, block_2_byte_1, block_2_byte_0}), .out(line_hit), .sel(way_sel));  // open: in3

  // Other names for the same wires on the sheet: offset[1:0] = cpu_addr[1:0]; tag[6:0] = cpu_addr[9:3];
  //   hit_way_0 = hit_way[0]; hit_way_1 = hit_way[1]; hit_way_2 = hit_way[2];
  //   line_0[31:0] = {block_0_byte_3, block_0_byte_2, block_0_byte_1, block_0_byte_0};
  //   line_1[31:0] = {block_1_byte_3, block_1_byte_2, block_1_byte_1, block_1_byte_0};
  //   line_2[31:0] = {block_2_byte_3, block_2_byte_2, block_2_byte_1, block_2_byte_0}; old_vec_0 = old_vec[0];
  //   old_vec_1 = old_vec[1]; old_vec_2 = old_vec[2]; w = w_en
endmodule

module sub_block (
  input  clk,
  input  [31:0] block_from_mem,
  input  hit_block,
  input  index,
  input  old,
  input  line_update_en,
  input  [7:0] byte_in,
  input  [1:0] offset,
  input  hit,
  input  wr,
  output [7:0] byte_out_0,
  output [7:0] byte_out_1,
  output [7:0] byte_out_2,
  output [7:0] byte_out_3
);

  wire and_1_out, and_2_out, and_3_out, and_4_out, and_5_out, and_6_out, and_7_out, and_8_out, and_9_out,
       and_10_out, and_11_out, and_12_out, b0, b1, b2, b3, en0, en1, en2, en3;
  wire [1:0] bitfinder_1_index, bitfinder_2_index, bitfinder_3_index, bitfinder_4_index;
  wire [2:0] and_13_out, and_14_out, and_15_out, and_16_out;
  wire [7:0] byte_wr0, byte_wr1, byte_wr2, byte_wr3;

  and and_1 (and_1_out, old, ~hit_block);  // AND_Gate
  and and_2 (and_2_out, hit, b0);
  and and_3 (and_3_out, old, ~hit_block);  // AND_Gate
  and and_4 (and_4_out, hit, b1);
  and and_5 (and_5_out, old, ~hit_block);  // AND_Gate
  and and_6 (and_6_out, hit, b2);
  and and_7 (and_7_out, old, ~hit_block);  // AND_Gate
  and and_8 (and_8_out, hit, b3);
  and and_9 (and_9_out, index, en0, line_update_en);
  and and_10 (and_10_out, index, en1, line_update_en);
  and and_11 (and_11_out, index, en2, line_update_en);
  and and_12 (and_12_out, index, en3, line_update_en);
  or or_1 (en0, and_1_out, and_2_out);
  or or_2 (en1, and_3_out, and_4_out);
  or or_3 (en2, and_5_out, and_6_out);
  or or_4 (en3, and_7_out, and_8_out);
  Register register_1 (.D(byte_wr0), .en(and_9_out), .clk(clk), .Q(byte_out_0));  // open: clr
  Register register_2 (.D(byte_wr1), .en(and_10_out), .clk(clk), .Q(byte_out_1));  // open: clr
  Register register_3 (.D(byte_wr2), .en(and_11_out), .clk(clk), .Q(byte_out_2));  // open: clr
  Register register_4 (.D(byte_wr3), .en(and_12_out), .clk(clk), .Q(byte_out_3));  // open: clr
  not not_1 (and_13_out[2], wr);
  not not_2 (and_13_out[1], hit_block);
  not not_3 (and_14_out[2], wr);
  not not_4 (and_14_out[1], hit_block);
  and and_13 (and_13_out[0], wr, b0);
  and and_14 (and_14_out[0], wr, b3);
  Multiplexer #(.enable("false"), .select(2), .width(8)) multiplexer_1 (
    .in0(byte_in), .in1(block_from_mem[7:0]), .in2(byte_out_0), .out(byte_wr0), .sel(bitfinder_1_index));  // open: in3
  BitFinder #(.width(3)) bitfinder_1 (.in(and_13_out), .index(bitfinder_1_index));  // open: found
  Multiplexer #(.enable("false"), .select(2), .width(8)) multiplexer_2 (
    .in0(byte_in), .in1(block_from_mem[31:24]), .in2(byte_out_3), .out(byte_wr3), .sel(bitfinder_2_index));  // open: in3
  BitFinder #(.width(3)) bitfinder_2 (.in(and_14_out), .index(bitfinder_2_index));  // open: found
  not not_5 (and_15_out[2], wr);
  not not_6 (and_15_out[1], hit_block);
  not not_7 (and_16_out[2], wr);
  not not_8 (and_16_out[1], hit_block);
  and and_15 (and_15_out[0], wr, b1);
  and and_16 (and_16_out[0], wr, b2);
  Multiplexer #(.enable("false"), .select(2), .width(8)) multiplexer_3 (
    .in0(byte_in), .in1(block_from_mem[15:8]), .in2(byte_out_1), .out(byte_wr1), .sel(bitfinder_3_index));  // open: in3
  BitFinder #(.width(3)) bitfinder_3 (.in(and_15_out), .index(bitfinder_3_index));  // open: found
  Multiplexer #(.enable("false"), .select(2), .width(8)) multiplexer_4 (
    .in0(byte_in), .in1(block_from_mem[23:16]), .in2(byte_out_2), .out(byte_wr2), .sel(bitfinder_4_index));  // open: in3
  BitFinder #(.width(3)) bitfinder_4 (.in(and_16_out), .index(bitfinder_4_index));  // open: found
  and and_17 (b3, offset[0], offset[1]);
  and and_18 (b2, ~offset[0], offset[1]);  // AND_Gate
  and and_19 (b1, offset[0], ~offset[1]);  // AND_Gate
  and and_20 (b0, ~offset[0], ~offset[1]);  // AND_Gate
  // Probe on byte_wr0
  // Probe on byte_wr1
  // Probe on byte_wr2
  // Probe on byte_wr3

  // Other names for the same wires on the sheet: byte_from_mem_0[7:0] = block_from_mem[7:0];
  //   byte_from_mem_1[7:0] = block_from_mem[15:8]; byte_from_mem_2[7:0] = block_from_mem[23:16];
  //   byte_from_mem_3[7:0] = block_from_mem[31:24]
endmodule

module FSM (
  input  wr,
  input  dirty,
  input  rd,
  input  w_en,
  input  hit,
  input  clk,
  output rd_mem,
  output age_initial,
  output wr_mem,
  output [5:0] cur_state,
  output ready,
  output cmd_store,
  output mem_data_store,
  output age_update,
  output line_update_en
);

  wire [5:0] next_state_gen_1_next_state;

  next_state_gen next_state_gen_1 (
    .next_state(next_state_gen_1_next_state), .cur_state(cur_state), .wr(wr), .rd(rd), .hit(hit),
    .dirty(dirty), .w_en(w_en));
  Register #(.width(6)) register_1 (.D(next_state_gen_1_next_state), .en(1'b1), .clk(clk), .Q(cur_state));  // open: clr
  state_out state_out_1 (
    .cur_state(cur_state), .rd_mem(rd_mem), .wr_mem(wr_mem), .ready(ready), .cmd_store(cmd_store),
    .age_update(age_update), .line_update_en(line_update_en), .age_initial(age_initial),
    .mem_data_store(mem_data_store));
endmodule

module next_state_gen (
  input  [5:0] cur_state,
  input  wr,
  input  dirty,
  input  rd,
  input  w_en,
  input  hit,
  output [5:0] next_state
);

  wire and_1_out, and_2_out, and_3_out, and_4_out, and_5_out, and_6_out, and_7_out, and_9_out, nor_1_out,
       not_1_out, or_1_out, or_2_out, or_3_out;

  and and_1 (and_1_out, w_en, hit);
  and and_2 (and_2_out, ~w_en, hit);  // AND_Gate
  or or_1 (or_1_out, wr, rd);
  nor nor_1 (nor_1_out, cur_state[0], cur_state[1], cur_state[2], cur_state[3], cur_state[4], cur_state[5]);
  and and_3 (and_3_out, and_1_out, cur_state[1]);
  and and_4 (and_4_out, w_en, ~dirty, cur_state[5]);  // AND_Gate
  and and_5 (and_5_out, and_2_out, cur_state[1]);
  and and_6 (and_6_out, ~w_en, ~dirty, cur_state[5]);  // AND_Gate
  and and_7 (and_7_out, ~w_en, cur_state[4]);  // AND_Gate
  and and_8 (next_state[1], or_1_out, cur_state[0]);
  or or_2 (or_2_out, and_3_out, and_4_out);
  or or_3 (or_3_out, and_5_out, and_6_out);
  or or_4 (next_state[0], nor_1_out, cur_state[2], cur_state[3]);
  or or_5 (next_state[3], or_3_out, and_7_out);
  or or_6 (next_state[2], or_2_out, and_9_out);
  and and_9 (and_9_out, w_en, cur_state[5]);
  not not_1 (not_1_out, hit);
  and and_10 (next_state[5], not_1_out, cur_state[1]);
  and and_11 (next_state[4], dirty, cur_state[5]);

  // Other names for the same wires on the sheet: READY = cur_state[0]; MATCH = cur_state[1]; WRITE = cur_state[2];
  //   READ = cur_state[3]; W_MEM = cur_state[4]; R_MEM = cur_state[5]; NEXT_READY = next_state[0];
  //   NEXT_MATCH = next_state[1]; NEXT_WRITE = next_state[2]; NEXT_READ = next_state[3]; NEXT_W_MEM = next_state[4];
  //   NEXT_R_MEM = next_state[5]
endmodule

module state_out (
  input  [5:0] cur_state,
  output rd_mem,
  output wr_mem,
  output ready,
  output cmd_store,
  output age_update,
  output line_update_en,
  output age_initial,
  output mem_data_store
);

  or or_1 (age_update, cur_state[2], cur_state[3]);
  or or_2 (mem_data_store, cur_state[4], cur_state[5]);
  // Probe on age_update
  // Probe on line_update_en
  or or_3 (line_update_en, cur_state[2], cur_state[3]);
  nor nor_1 (age_initial, cur_state[0], cur_state[1], cur_state[2], cur_state[3], cur_state[4], cur_state[5]);
  or or_4 (ready, cur_state[2], age_initial, cur_state[3]);
  or or_5 (cmd_store, cur_state[2], age_initial, cur_state[3]);
  // Probe on ready
  // Probe on cmd_store

  assign rd_mem = cur_state[5];
  assign wr_mem = cur_state[4];

  // Other names for the same wires on the sheet: READY_t = cur_state[0]; MATCH = cur_state[1]; WRITE = cur_state[2];
  //   READ = cur_state[3]; W_MEM = cur_state[4]; R_MEM = cur_state[5]
endmodule

module hit_cmp (
  input  [6:0] tag_0,
  input  [6:0] tag_1,
  input  [6:0] tag_2,
  input  [6:0] tag,
  input  index,
  input  valid_0,
  input  valid_1,
  input  valid_2,
  output [2:0] hit_way,
  output hit
);

  wire comparator_1_eq, comparator_2_eq, comparator_3_eq;

  Comparator #(.mode("unsigned"), .width(7)) comparator_1 (.a(tag_0), .b(tag), .eq(comparator_1_eq));  // open: gt, lt
  Comparator #(.mode("unsigned"), .width(7)) comparator_2 (.a(tag_1), .b(tag), .eq(comparator_2_eq));  // open: gt, lt
  Comparator #(.mode("unsigned"), .width(7)) comparator_3 (.a(tag_2), .b(tag), .eq(comparator_3_eq));  // open: gt, lt
  and and_1 (hit_way[0], valid_0, comparator_1_eq);
  and and_2 (hit_way[1], valid_1, comparator_2_eq);
  and and_3 (hit_way[2], valid_2, comparator_3_eq);
  or or_1 (hit, hit_way[0], hit_way[1], hit_way[2]);
endmodule

module LRU (
  input  index,
  input  [2:0] hit_way,
  input  hit,
  input  update_en,
  input  clk,
  input  age_initial,
  output [1:0] age_0,
  output [1:0] age_1,
  output [1:0] age_2,
  output [2:0] old_vec
);

  wire and_1_out, and_2_out, update_en_0, update_en_1;
  wire [1:0] adder_1_out, adder_2_out, adder_3_out, adder_4_out, adder_5_out, adder_6_out, age_0_0, age_0_1,
       age_0_2, age_1_0, age_1_1, age_1_2, age_sel, bitfinder_1_index, bitfinder_2_index, bitfinder_3_index,
       bitfinder_4_index, bitfinder_5_index, bitfinder_6_index, bitfinder_7_index, multiplexer_1_out,
       multiplexer_2_out, multiplexer_3_out, multiplexer_4_out, multiplexer_6_out, multiplexer_7_out,
       multiplexer_8_out, multiplexer_9_out, multiplexer_10_out, multiplexer_11_out, multiplexer_12_out,
       multiplexer_13_out, multiplexer_14_out, multiplexer_15_out, multiplexer_16_out, multiplexer_17_out;
  wire [2:0] comparator_1_lt, comparator_2_lt, comparator_3_lt, comparator_4_lt, comparator_5_lt,
       comparator_6_lt;

  Multiplexer #(.enable("false"), .width(2)) multiplexer_1 (
    .in0(age_0_0), .in1(age_1_0), .out(multiplexer_1_out), .sel(index));
  Multiplexer #(.enable("false"), .width(2)) multiplexer_2 (
    .in0(age_0_1), .in1(age_1_1), .out(multiplexer_2_out), .sel(index));
  Multiplexer #(.enable("false"), .width(2)) multiplexer_3 (
    .in0(age_0_2), .in1(age_1_2), .out(multiplexer_3_out), .sel(index));
  Multiplexer #(.enable("false"), .select(2), .width(2)) multiplexer_4 (
    .in0(multiplexer_1_out), .in1(multiplexer_2_out), .in2(multiplexer_3_out), .out(multiplexer_4_out),
    .sel(bitfinder_1_index));  // open: in3
  BitFinder #(.width(3)) bitfinder_1 (.in(hit_way), .index(bitfinder_1_index));  // open: found
  // Probe on age_sel
  Multiplexer #(.enable("false"), .width(2)) multiplexer_5 (
    .in0(2'b10), .in1(multiplexer_4_out), .out(age_sel), .sel(hit));
  Comparator #(.mode("unsigned"), .width(2)) comparator_1 (
    .a(age_0_0), .b(age_sel), .gt(comparator_1_lt[2]), .eq(comparator_1_lt[1]), .lt(comparator_1_lt[0]));
  Comparator #(.mode("unsigned"), .width(2)) comparator_2 (
    .a(age_0_1), .b(age_sel), .gt(comparator_2_lt[2]), .eq(comparator_2_lt[1]), .lt(comparator_2_lt[0]));
  Comparator #(.mode("unsigned"), .width(2)) comparator_3 (
    .a(age_0_2), .b(age_sel), .gt(comparator_3_lt[2]), .eq(comparator_3_lt[1]), .lt(comparator_3_lt[0]));
  Comparator #(.mode("unsigned"), .width(2)) comparator_4 (
    .a(age_1_0), .b(age_sel), .gt(comparator_4_lt[2]), .eq(comparator_4_lt[1]), .lt(comparator_4_lt[0]));
  Comparator #(.mode("unsigned"), .width(2)) comparator_5 (
    .a(age_1_1), .b(age_sel), .gt(comparator_5_lt[2]), .eq(comparator_5_lt[1]), .lt(comparator_5_lt[0]));
  Comparator #(.mode("unsigned"), .width(2)) comparator_6 (
    .a(age_1_2), .b(age_sel), .gt(comparator_6_lt[2]), .eq(comparator_6_lt[1]), .lt(comparator_6_lt[0]));
  BitFinder #(.width(3)) bitfinder_2 (.in(comparator_6_lt), .index(bitfinder_2_index));  // open: found
  and and_1 (and_1_out, update_en, index);
  and and_2 (and_2_out, update_en, ~index);  // AND_Gate
  Adder #(.width(2)) adder_1 (.a(age_0_0), .b(2'b01), .out(adder_1_out));  // open: cin, cout
  BitFinder #(.width(3)) bitfinder_3 (.in(comparator_1_lt), .index(bitfinder_3_index));  // open: found
  Adder #(.width(2)) adder_2 (.a(age_0_1), .b(2'b01), .out(adder_2_out));  // open: cin, cout
  BitFinder #(.width(3)) bitfinder_4 (.in(comparator_2_lt), .index(bitfinder_4_index));  // open: found
  Adder #(.width(2)) adder_3 (.a(age_0_2), .b(2'b01), .out(adder_3_out));  // open: cin, cout
  BitFinder #(.width(3)) bitfinder_5 (.in(comparator_3_lt), .index(bitfinder_5_index));  // open: found
  Adder #(.width(2)) adder_4 (.a(age_1_0), .b(2'b01), .out(adder_4_out));  // open: cin, cout
  BitFinder #(.width(3)) bitfinder_6 (.in(comparator_4_lt), .index(bitfinder_6_index));  // open: found
  Adder #(.width(2)) adder_5 (.a(age_1_1), .b(2'b01), .out(adder_5_out));  // open: cin, cout
  BitFinder #(.width(3)) bitfinder_7 (.in(comparator_5_lt), .index(bitfinder_7_index));  // open: found
  Adder #(.width(2)) adder_6 (.a(age_1_2), .b(2'b01), .out(adder_6_out));  // open: cin, cout
  or or_1 (update_en_1, and_1_out, age_initial);
  // Probe on multiplexer_6_out
  Multiplexer #(.enable("false"), .select(2), .width(2)) multiplexer_6 (
    .in0(adder_1_out), .in1(2'b00), .in2(age_0_0), .in3(2'b00), .out(multiplexer_6_out),
    .sel(multiplexer_7_out));
  Multiplexer #(.enable("false"), .width(2)) multiplexer_7 (
    .in0(bitfinder_3_index), .in1(2'b11), .out(multiplexer_7_out), .sel(age_initial));
  Multiplexer #(.enable("false"), .select(2), .width(2)) multiplexer_8 (
    .in0(adder_2_out), .in1(2'b00), .in2(age_0_1), .in3(2'b01), .out(multiplexer_8_out),
    .sel(multiplexer_9_out));
  Multiplexer #(.enable("false"), .width(2)) multiplexer_9 (
    .in0(bitfinder_4_index), .in1(2'b11), .out(multiplexer_9_out), .sel(age_initial));
  Multiplexer #(.enable("false"), .select(2), .width(2)) multiplexer_10 (
    .in0(adder_3_out), .in1(2'b00), .in2(age_0_2), .in3(2'b10), .out(multiplexer_10_out),
    .sel(multiplexer_11_out));
  Multiplexer #(.enable("false"), .width(2)) multiplexer_11 (
    .in0(bitfinder_5_index), .in1(2'b11), .out(multiplexer_11_out), .sel(age_initial));
  Multiplexer #(.enable("false"), .select(2), .width(2)) multiplexer_12 (
    .in0(adder_4_out), .in1(2'b00), .in2(age_1_0), .in3(2'b00), .out(multiplexer_12_out),
    .sel(multiplexer_13_out));
  Multiplexer #(.enable("false"), .width(2)) multiplexer_13 (
    .in0(bitfinder_6_index), .in1(2'b11), .out(multiplexer_13_out), .sel(age_initial));
  Multiplexer #(.enable("false"), .select(2), .width(2)) multiplexer_14 (
    .in0(adder_5_out), .in1(2'b00), .in2(age_1_1), .in3(2'b01), .out(multiplexer_14_out),
    .sel(multiplexer_15_out));
  Multiplexer #(.enable("false"), .width(2)) multiplexer_15 (
    .in0(bitfinder_7_index), .in1(2'b11), .out(multiplexer_15_out), .sel(age_initial));
  Multiplexer #(.enable("false"), .select(2), .width(2)) multiplexer_16 (
    .in0(adder_6_out), .in1(2'b00), .in2(age_1_2), .in3(2'b10), .out(multiplexer_16_out),
    .sel(multiplexer_17_out));
  Multiplexer #(.enable("false"), .width(2)) multiplexer_17 (
    .in0(bitfinder_2_index), .in1(2'b11), .out(multiplexer_17_out), .sel(age_initial));
  or or_2 (update_en_0, and_2_out, age_initial);
  Register #(.width(2)) register_1 (.D(multiplexer_6_out), .en(update_en_0), .clk(clk), .Q(age_0_0), .clr(1'b0));
  Register #(.width(2)) register_2 (.D(multiplexer_8_out), .en(update_en_0), .clk(clk), .Q(age_0_1), .clr(1'b0));
  Register #(.width(2)) register_3 (.D(multiplexer_10_out), .en(update_en_0), .clk(clk), .Q(age_0_2), .clr(1'b0));
  Register #(.width(2)) register_4 (.D(multiplexer_12_out), .en(update_en_1), .clk(clk), .Q(age_1_0), .clr(1'b0));
  Register #(.width(2)) register_5 (.D(multiplexer_14_out), .en(update_en_1), .clk(clk), .Q(age_1_1), .clr(1'b0));
  Register #(.width(2)) register_6 (.D(multiplexer_16_out), .en(update_en_1), .clk(clk), .Q(age_1_2), .clr(1'b0));
  Multiplexer #(.enable("false"), .width(2)) multiplexer_18 (.in0(age_0_0), .in1(age_1_0), .out(age_0), .sel(index));
  Multiplexer #(.enable("false"), .width(2)) multiplexer_19 (.in0(age_0_1), .in1(age_1_1), .out(age_1), .sel(index));
  Multiplexer #(.enable("false"), .width(2)) multiplexer_20 (.in0(age_0_2), .in1(age_1_2), .out(age_2), .sel(index));
  and and_3 (old_vec[0], ~age_0[0], age_0[1]);  // AND_Gate
  and and_4 (old_vec[1], ~age_1[0], age_1[1]);  // AND_Gate
  and and_5 (old_vec[2], ~age_2[0], age_2[1]);  // AND_Gate
  // Probe on age_0_0
  // Probe on age_0_1
  // Probe on age_0_2
  // Probe on age_1_0
  // Probe on age_1_1
  // Probe on age_1_2

  // Other names for the same wires on the sheet: update = update_en
endmodule
