// Logisim project bcd.circ as structural Verilog: 1 circuit, main circuit implementation
module implementation (
  input  w3,
  input  w2,
  input  w1,
  input  w0,
  output a,
  output b,
  output c,
  output d,
  output e,
  output f,
  output g
);

  wire and_1_out, and_2_out, and_3_out, and_4_out, and_5_out, and_6_out, and_7_out, and_8_out, and_9_out,
       and_10_out, and_11_out, and_12_out, and_13_out, and_14_out, and_15_out, and_16_out, Notw0t, Notw1t,
       Notw2t, Notw3t;

  not not_1 (Notw3t, w3);
  not not_2 (Notw2t, w2);
  not not_3 (Notw1t, w1);
  not not_4 (Notw0t, w0);
  and and_1 (and_1_out, Notw2t, Notw0t);
  and and_2 (and_2_out, w2, w0);
  and and_3 (and_3_out, Notw1t, Notw0t);
  and and_4 (and_4_out, w1, w0);
  and and_5 (and_5_out, Notw2t, Notw0t);
  and and_6 (and_6_out, Notw2t, w1);
  and and_7 (and_7_out, w2, Notw1t, w0);
  and and_8 (and_8_out, w1, Notw0t);
  and and_9 (and_9_out, Notw2t, Notw0t);
  and and_10 (and_10_out, w1, Notw0t);
  and and_11 (and_11_out, Notw1t, Notw0t);
  and and_12 (and_12_out, w2, Notw1t);
  and and_13 (and_13_out, w2, Notw0t);
  and and_14 (and_14_out, w1, Notw2t);
  and and_15 (and_15_out, w2, Notw1t);
  and and_16 (and_16_out, w2, Notw0t);
  or or_1 (a, and_1_out, w1, and_2_out, w3);
  or or_2 (b, Notw2t, and_3_out, and_4_out);
  or or_3 (c, Notw1t, w2, w0);
  or or_4 (d, and_5_out, and_6_out, and_7_out, and_8_out, w3);
  or or_5 (e, and_9_out, and_10_out);
  or or_6 (f, and_11_out, and_12_out, and_13_out, w3);
  or or_7 (g, and_14_out, and_15_out, w3, and_16_out);

  // Other names for the same wires on the sheet: at = a; bt = b; ct = c; dt = d; et = e; ft = f; gt = g; w0t = w0;
  //   w1t = w1; w2t = w2; w3t = w3

  // Notes on the sheet:
  //   a
  //   b
  //   c
  //   d
  //   e
  //   f
  //   g
endmodule
