// Logisim project fun.circ as structural Verilog: 1 circuit, main circuit implementation
module implementation (
  input  x3,
  input  x2,
  input  x1,
  input  x0,
  output the_output
);

  wire and_1_out, and_2_out;

  and and_1 (and_1_out, x0, x1);
  and and_2 (and_2_out, x2, x3);
  or or_1 (the_output, and_1_out, and_2_out);

  // Other names for the same wires on the sheet: the_output_t = the_output; x0t = x0; x1t = x1; x2t = x2; x3t = x3
endmodule
