// Logisim project adder4.circ as structural Verilog: 1 circuit, main circuit implementation
module implementation (
  input  [3:0] Ain,
  input  [3:0] Bin,
  input  Cinin,
  output [3:0] Sum_Out,
  output Carry_Out
);

  wire and_5_out, and_6_out, and_7_out, and_8_out, and_9_out, and_10_out, and_11_out, C0, C1, C2, G00, G01,
       G02, G03, G11, G12, G13, P00, P01, P02, P03, P11, P12, P13;

  and and_1 (G00, Ain[0], Bin[0]);
  and and_2 (G01, Ain[1], Bin[1]);
  and and_3 (G02, Ain[2], Bin[2]);
  and and_4 (G03, Ain[3], Bin[3]);
  and and_5 (and_5_out, G00, P01);
  and and_6 (and_6_out, G11, P02);
  and and_7 (and_7_out, G12, P03);
  and and_8 (and_8_out, P00, Cinin);
  and and_9 (and_9_out, P11, C0);
  and and_10 (and_10_out, P12, C1);
  and and_11 (and_11_out, P13, C2);
  xor xor_1 (Sum_Out[0], P00, Cinin);
  xor xor_2 (Sum_Out[1], P01, C0);
  xor xor_3 (Sum_Out[2], P02, C1);
  xor xor_4 (Sum_Out[3], P03, C2);
  or or_1 (G11, and_5_out, G01);
  or or_2 (G12, and_6_out, G02);
  or or_3 (G13, and_7_out, G03);
  or or_4 (C0, G00, and_8_out);
  or or_5 (C1, G11, and_9_out);
  or or_6 (C2, G12, and_10_out);
  or or_7 (Carry_Out, G13, and_11_out);
  xor xor_5 (P00, Ain[0], Bin[0]);
  xor xor_6 (P01, Ain[1], Bin[1]);
  xor xor_7 (P02, Ain[2], Bin[2]);
  xor xor_8 (P03, Ain[3], Bin[3]);
  and and_12 (P11, P00, P01);
  and and_13 (P12, P02, P11);
  and and_14 (P13, P03, P12);

  // Other names for the same wires on the sheet: A[3:0] = Ain; A0 = Ain[0]; A1 = Ain[1]; A2 = Ain[2]; A3 = Ain[3];
  //   B[3:0] = Bin; B0 = Bin[0]; B1 = Bin[1]; B2 = Bin[2]; B3 = Bin[3]; C3 = Carry_Out; Cin = Cinin; G10 = G00;
  //   P10 = P00; Sum[3:0] = Sum_Out; Sum0 = Sum_Out[0]; Sum1 = Sum_Out[1]; Sum2 = Sum_Out[2]; Sum3 = Sum_Out[3]
endmodule
