// Logisim project shifter.circ as structural Verilog: 1 circuit, main circuit implementation
module implementation (
  input  IsRightShiftIn,
  input  IsArithmeticIn,
  input  [1:0] ShiftAmountIn,
  input  [2:0] NumberIn,
  output [2:0] ShiftedNumberOut
);

  wire A0, A1, A2, left0, left1, left2, Right0, Right1, Right2;

  Multiplexer #(.enable("false"), .select(2)) multiplexer_1 (
    .in0(NumberIn[0]), .in1(1'b0), .in2(1'b0), .in3(1'b0), .out(left0), .sel(ShiftAmountIn));
  Multiplexer #(.enable("false"), .select(2)) multiplexer_2 (
    .in0(NumberIn[1]), .in1(NumberIn[0]), .in2(1'b0), .in3(1'b0), .out(left1), .sel(ShiftAmountIn));
  Multiplexer #(.enable("false"), .select(2)) multiplexer_3 (
    .in0(NumberIn[2]), .in1(NumberIn[1]), .in2(NumberIn[0]), .in3(1'b0), .out(left2), .sel(ShiftAmountIn));
  Multiplexer #(.enable("false"), .select(2)) multiplexer_4 (
    .in0(NumberIn[2]), .in1(1'b0), .in2(1'b0), .in3(1'b0), .out(Right2), .sel(ShiftAmountIn));
  Multiplexer #(.enable("false"), .select(2)) multiplexer_5 (
    .in0(NumberIn[1]), .in1(NumberIn[2]), .in2(1'b0), .in3(1'b0), .out(Right1), .sel(ShiftAmountIn));
  Multiplexer #(.enable("false"), .select(2)) multiplexer_6 (
    .in0(NumberIn[0]), .in1(NumberIn[1]), .in2(NumberIn[2]), .in3(1'b0), .out(Right0), .sel(ShiftAmountIn));
  Multiplexer #(.enable("false"), .select(2)) multiplexer_7 (
    .in0(NumberIn[0]), .in1(NumberIn[1]), .in2(NumberIn[2]), .in3(NumberIn[2]), .out(A0), .sel(ShiftAmountIn));
  Multiplexer #(.enable("false"), .select(2)) multiplexer_8 (
    .in0(NumberIn[1]), .in1(NumberIn[2]), .in2(NumberIn[2]), .in3(NumberIn[2]), .out(A1), .sel(ShiftAmountIn));
  Multiplexer #(.enable("false"), .select(2)) multiplexer_9 (
    .in0(NumberIn[2]), .in1(NumberIn[2]), .in2(NumberIn[2]), .in3(NumberIn[2]), .out(A2), .sel(ShiftAmountIn));
  Multiplexer #(.enable("false"), .select(2), .width(3)) multiplexer_10 (
    .in0({left2, left1, left0}), .in1({left2, left1, left0}), .in2({Right2, Right1, Right0}),
    .in3({A2, A1, A0}), .out(ShiftedNumberOut), .sel({IsRightShiftIn, IsArithmeticIn}));

  // Other names for the same wires on the sheet: IsArithmetic = IsArithmeticIn; IsRightShift = IsRightShiftIn;
  //   Number[2:0] = NumberIn; Number0 = NumberIn[0]; Number1 = NumberIn[1]; Number2 = NumberIn[2];
  //   ShiftAmount[1:0] = ShiftAmountIn; ShiftedNumber[2:0] = ShiftedNumberOut

  // Notes on the sheet:
  //   Miou Lu
  //   Shuhao Gao
endmodule
