// Logisim project FourBitParity.circ as structural Verilog: 3 circuits, main circuit implementation
module implementation (
  input  EnableIn,
  input  InputBitIn,
  input  ClkIn,
  output IsEvenOut
);

  wire [3:0] nextstate_1_p0_out, register_1_q;

  // Probe on register_1_q
  // Probe on nextstate_1_p0_out
  NextState nextstate_1 (
    .p3(register_1_q[3]), .p2(register_1_q[2]), .p1(register_1_q[1]), .p0(register_1_q[0]),
    .InputBit(InputBitIn), .p3_out(nextstate_1_p0_out[3]), .p2_out(nextstate_1_p0_out[2]),
    .p1_out(nextstate_1_p0_out[1]), .p0_out(nextstate_1_p0_out[0]));
  Register #(.width(4)) register_1 (.D(nextstate_1_p0_out), .en(EnableIn), .clk(ClkIn), .Q(register_1_q));  // open: clr
  Output output_1 (
    .P3(register_1_q[3]), .P2(register_1_q[2]), .P1(register_1_q[1]), .P0(register_1_q[0]),
    .BitOutput(IsEvenOut));

  // Other names for the same wires on the sheet: Clk = ClkIn; Enable = EnableIn; InputBit = InputBitIn
endmodule

module NextState (
  input  p3,
  input  p2,
  input  p1,
  input  p0,
  input  InputBit,
  output p3_out,
  output p2_out,
  output p1_out,
  output p0_out
);

  wire and_1_out, and_2_out, and_3_out, and_4_out, and_5_out, and_6_out, and_7_out, and_8_out, and_9_out,
       and_10_out, and_11_out, and_12_out, and_13_out, and_14_out, and_15_out, and_16_out, and_17_out,
       and_18_out, NOTinput, NOTp0, NOTp1, NOTp2, NOTp3;

  and and_1 (and_1_out, p2, p1, NOTp0, NOTinput);
  and and_2 (and_2_out, p2, p1, p0, InputBit);
  and and_3 (and_3_out, p3, p1, NOTp0, NOTinput);
  and and_4 (and_4_out, p3, p2, p0, InputBit);
  and and_5 (and_5_out, p3, p2, NOTp0, NOTinput);
  not not_1 (NOTp3, p3);
  not not_2 (NOTp2, p2);
  not not_3 (NOTp1, p1);
  not not_4 (NOTp0, p0);
  not not_5 (NOTinput, InputBit);
  or or_1 (p3_out, and_1_out, and_2_out, and_3_out, and_4_out, and_5_out);
  and and_6 (and_6_out, NOTp2, p1);
  and and_7 (and_7_out, NOTp3, p2, NOTp1);
  and and_8 (and_8_out, p2, NOTp1, p0, NOTinput);
  or or_2 (p2_out, and_6_out, and_7_out, and_8_out);
  and and_9 (and_9_out, NOTp3, NOTp1);
  and and_10 (and_10_out, NOTp2, NOTp1, NOTp0);
  and and_11 (and_11_out, p2, NOTp1, p0, NOTinput);
  or or_3 (p1_out, and_9_out, and_10_out, and_11_out);
  and and_12 (and_12_out, NOTp3, NOTp2, NOTp1, InputBit);
  and and_13 (and_13_out, NOTp3, NOTp0, InputBit);
  and and_14 (and_14_out, NOTp2, NOTp0, InputBit);
  and and_15 (and_15_out, NOTp3, p1, p0, NOTinput);
  and and_16 (and_16_out, p2, p0, NOTinput);
  and and_17 (and_17_out, p3, NOTp2, p1, NOTp0);
  and and_18 (and_18_out, p3, p2, NOTp1, NOTinput);
  or or_4 (p0_out, and_12_out, and_13_out, and_14_out, and_15_out, and_16_out, and_17_out, and_18_out);
endmodule

module Output (
  input  P3,
  input  P2,
  input  P1,
  input  P0,
  output BitOutput
);


  assign BitOutput = P3;
endmodule
