// Logisim project UpDownCounter.circ as structural Verilog: 2 circuits, main circuit implementation
module implementation (
  input  EnableIn,
  input  CountUpIn,
  input  CountDownIn,
  input  clkIn,
  output [2:0] Count
);

  wire [2:0] updowncounter_1_output0;

  UpDownCounter updowncounter_1 (
    .input2(Count[2]), .input1(Count[1]), .input0(Count[0]), .countup(CountUpIn), .countdown(CountDownIn),
    .output2(updowncounter_1_output0[2]), .output1(updowncounter_1_output0[1]),
    .output0(updowncounter_1_output0[0]));
  Register #(.width(3)) register_1 (.D(updowncounter_1_output0), .en(EnableIn), .clk(clkIn), .Q(Count));  // open: clr

  // Other names for the same wires on the sheet: clk = clkIn; CountDown = CountDownIn; CountUp = CountUpIn;
  //   Enable = EnableIn
endmodule

module UpDownCounter (
  input  input2,
  input  input1,
  input  input0,
  input  countup,
  input  countdown,
  output output2,
  output output1,
  output output0
);

  wire and_1_out, and_2_out, and_3_out, and_4_out, and_5_out, and_6_out, and_7_out, and_8_out, and_9_out,
       and_10_out, and_11_out, and_12_out, and_13_out, and_14_out, not_1_out, not_2_out, not_3_out, not_4_out;

  not not_1 (not_1_out, input1);
  not not_2 (not_2_out, input0);
  not not_3 (not_3_out, countup);
  not not_4 (not_4_out, countdown);
  and and_1 (and_1_out, input1, input0, countup, not_4_out);
  and and_2 (and_2_out, input2, not_4_out);
  and and_3 (and_3_out, input2, input0);
  and and_4 (and_4_out, input2, input1);
  and and_5 (and_5_out, not_1_out, input0, countup, not_4_out);
  and and_6 (and_6_out, input1, not_2_out, not_4_out);
  and and_7 (and_7_out, input1, input0, not_3_out);
  and and_8 (and_8_out, input2, not_1_out, not_2_out, countdown);
  and and_9 (and_9_out, input2, input1, not_4_out);
  and and_10 (and_10_out, not_2_out, countup);
  and and_11 (and_11_out, input0, not_3_out, not_4_out);
  and and_12 (and_12_out, input1, not_2_out, countdown);
  and and_13 (and_13_out, input2, not_2_out, countdown);
  and and_14 (and_14_out, input2, input1, input0, not_4_out);
  or or_1 (output2, and_1_out, and_2_out, and_3_out, and_4_out);
  or or_2 (output1, and_5_out, and_6_out, and_7_out, and_8_out, and_9_out);
  or or_3 (output0, and_10_out, and_11_out, and_12_out, and_13_out, and_14_out);
endmodule
