// Logisim project Vending.circ as structural Verilog: 3 circuits, main circuit implementation
module implementation (
  input  EnableIn,
  input  QuarterReceivedIn,
  input  DimeReceivedIn,
  input  NickelReceivedIn,
  input  ClkIn,
  output Give_Mechandise_Out,
  output Give_Dime_Out,
  output Give_Nickel_Out
);

  wire [2:0] register_1_q, vending_1_bit0_out;

  vending vending_1 (
    .bit2(register_1_q[2]), .bit1(register_1_q[1]), .bit0(register_1_q[0]),
    .QuarterReceive(QuarterReceivedIn), .DimeReceive(DimeReceivedIn), .NickelReceive(NickelReceivedIn),
    .bit2_out(vending_1_bit0_out[2]), .bit1_out(vending_1_bit0_out[1]), .bit0_out(vending_1_bit0_out[0]));
  Register #(.width(3)) register_1 (.D(vending_1_bit0_out), .en(EnableIn), .clk(ClkIn), .Q(register_1_q));  // open: clr
  Bits bits_1 (
    .bit2(register_1_q[2]), .bit1(register_1_q[1]), .bit0(register_1_q[0]),
    .QuarterReceive(QuarterReceivedIn), .DimeReceive(DimeReceivedIn), .NickelReceive(NickelReceivedIn),
    .Merchandise_Out(Give_Mechandise_Out), .Nickle_Out(Give_Nickel_Out), .Dime_out(Give_Dime_Out));

  // Other names for the same wires on the sheet: clk = ClkIn; DimeReceieved = DimeReceivedIn; Enable = EnableIn;
  //   Give_Dime = Give_Dime_Out; Give_Merchandise = Give_Mechandise_Out; Give_Nickel = Give_Nickel_Out;
  //   NickelReceieved = NickelReceivedIn; QuarterReceieved = QuarterReceivedIn
endmodule

module vending (
  input  bit2,
  input  bit1,
  input  bit0,
  input  QuarterReceive,
  input  DimeReceive,
  input  NickelReceive,
  output bit2_out,
  output bit1_out,
  output bit0_out
);

  wire and_1_out, and_2_out, and_3_out, and_4_out, and_5_out, and_6_out, and_7_out, and_8_out, and_9_out,
       and_10_out, and_11_out, and_12_out, and_13_out, Nbit0, Nbit1, Nbit2, NDime, NNickel, NQuarter;

  and and_1 (and_1_out, DimeReceive, bit1);
  and and_2 (and_2_out, bit1, bit0, NickelReceive);
  and and_3 (and_3_out, Nbit2, Nbit1, Nbit0, QuarterReceive);
  and and_4 (and_4_out, bit2, Nbit0, NQuarter, NDime);
  and and_5 (and_5_out, bit2, Nbit1, NQuarter, NDime, NNickel);
  not not_1 (Nbit2, bit2);
  not not_2 (Nbit1, bit1);
  not not_3 (Nbit0, bit0);
  not not_4 (NQuarter, QuarterReceive);
  not not_5 (NDime, DimeReceive);
  not not_6 (NNickel, NickelReceive);
  or or_1 (bit2_out, and_1_out, and_2_out, and_3_out, and_4_out, and_5_out);
  and and_6 (and_6_out, Nbit2, Nbit1, DimeReceive);
  and and_7 (and_7_out, bit1, Nbit0, NickelReceive);
  and and_8 (and_8_out, Nbit2, Nbit1, bit0, NickelReceive);
  and and_9 (and_9_out, bit1, NQuarter, NDime, NNickel);
  or or_2 (bit1_out, and_6_out, and_7_out, and_8_out, and_9_out);
  and and_10 (and_10_out, Nbit0, NickelReceive);
  and and_11 (and_11_out, Nbit2, Nbit1, Nbit0, QuarterReceive);
  and and_12 (and_12_out, Nbit2, bit0, NQuarter, NNickel);
  and and_13 (and_13_out, Nbit1, bit0, NQuarter, NDime, NNickel);
  or or_3 (bit0_out, and_10_out, and_11_out, and_12_out, and_13_out);

  // Other names for the same wires on the sheet: Dime = DimeReceive; Nickel = NickelReceive; Quarter = QuarterReceive
endmodule

module Bits (
  input  bit2,
  input  bit1,
  input  bit0,
  input  QuarterReceive,
  input  DimeReceive,
  input  NickelReceive,
  output Merchandise_Out,
  output Nickle_Out,
  output Dime_out
);

  wire and_1_out, and_2_out, and_3_out, and_4_out, and_5_out, and_6_out, and_7_out, and_8_out, and_9_out,
       and_10_out, Nbit0, Nbit1, Nbit2, NDime, NNickel, NQuarter;

  and and_1 (and_1_out, bit0, QuarterReceive);
  and and_2 (and_2_out, bit1, QuarterReceive);
  and and_3 (and_3_out, bit2, QuarterReceive);
  and and_4 (and_4_out, bit2, DimeReceive);
  and and_5 (and_5_out, bit0, bit2, NickelReceive);
  or or_1 (Merchandise_Out, and_1_out, and_2_out, and_3_out, and_4_out, and_5_out);
  not not_1 (Nbit2, bit2);
  not not_2 (Nbit1, bit1);
  not not_3 (Nbit0, bit0);
  not not_4 (NQuarter, QuarterReceive);
  not not_5 (NDime, DimeReceive);
  not not_6 (NNickel, NickelReceive);
  and and_6 (and_6_out, bit1, Nbit0, QuarterReceive);
  and and_7 (and_7_out, bit2, QuarterReceive);
  and and_8 (and_8_out, bit2, bit0, DimeReceive);
  or or_2 (Nickle_Out, and_6_out, and_7_out, and_8_out);
  and and_9 (and_9_out, bit1, bit0, QuarterReceive);
  and and_10 (and_10_out, bit2, QuarterReceive);
  or or_3 (Dime_out, and_9_out, and_10_out);

  // Other names for the same wires on the sheet: Dime = DimeReceive; Nickel = NickelReceive; Quarter = QuarterReceive
endmodule
